# Fritzing sketch Button2 (saved by Fritzing 0.9.2b)
circuit board: 3.3cm x 3cm
breadboards: 1

parts:
  R4 = Resistor [tolerance=±5% resistance=4.7k package=THT]
  R3 = Resistor [tolerance=±5% resistance=4.7k package=THT]
  Q1 = NPN-Transistor [package="TO92 [THT]"]
  J2 = male pin header, 8 pins [form="♂ (male)"]
  J1 = male pin header, 8 pins [form="♂ (male)"]
  U2 = attiny85 [package=dip]
  LED1 = LED - 3mm [color="Red (633nm)" package="3 mm [THT]"]  # not connected
  VCC1 = Battery
  J3 = male pin header, 3 pins [form="♂ (male)"]
  U3 = Voltage Regulator - 3.3V [package="TO220 [THT]"]

nets (from the pcb view):
  N1: R4.Pin_0, J1.pin5, U2.Pin_5
  N2: R4.Pin_1, R3.Pin_1, J2.pin1, J2.pin6, J1.pin3, U2.Pin_8, J3.pin2
  N3: R3.Pin_0, J1.pin6, U2.Pin_7
  N4: Q1.E, J1.pin1, U2.Pin_4, VCC1.-, U3.GND
  N5: Q1.B, U2.Pin_3
  N6: Q1.C, J2.pin5, J2.pin8
  N7: VCC1.+, J3.pin1, U3.input_voltage
  N8: J3.pin3, U3.output_voltage
