# Fritzing sketch Buttonsmall (saved by Fritzing 0.9.2b)
circuit board: 3.3cm x 3cm
breadboards: 1

parts:
  Q1 = NPN-Transistor [package="TO92 [THT]"]
  J2 = male pin header, 8 pins [form="♂ (male)"]
  J1 = male pin header, 8 pins [form="♂ (male)"]
  VCC1 = Battery
  2AA = male pin header, 3 pins [form="♂ (male)"]
  U3 = Voltage Regulator - 3.3V [package="TO220 [THT]"]
  Tiny = attiny85 [package=dip]
  R1 = Resistor [tolerance=±5% resistance=220 package="0805 [SMD]"]
  LED1 = LED - 3mm [color="Red (633nm)" package="3 mm [THT]"]
  C1 = Ceramic Capacitor [capacitance=1µF package="100 mil [THT, multilayer]"]
  R2 = Resistor [tolerance=±5% resistance=220 package="0805 [SMD]"]
  R3 = Resistor [tolerance=±5% resistance=220 package="0805 [SMD]"]
  R4 = Resistor [tolerance=±5% resistance=220 package="0805 [SMD]"]

nets (from the pcb view):
  N1: Q1.B, Tiny.Pin_3
  N2: Q1.C, J2.pin5, J2.pin8
  N3: J2.pin1, J2.pin6, J1.pin3, 2AA.pin2, Tiny.Pin_8, R2.Pin_1, R3.Pin_0, R4.Pin_0
  N4: J1.pin5, Tiny.Pin_5, R3.Pin_1
  N5: J1.pin6, Tiny.Pin_7, R4.Pin_1
  N6: VCC1.-, U3.GND
  N7: VCC1.+, 2AA.pin3, U3.input_voltage
  N8: 2AA.pin1, U3.output_voltage, C1.0
  N9: Tiny.Pin_2, R1.Pin_1
  N10: R1.Pin_0, LED1.anode

notes:
  pullup
